# Fritzing sketch pmSensorAttachedNoWifi (saved by Fritzing 0.9.9b)
breadboards: 1

parts:
  M1 = Arduino Uno WIFI REV2
  U1 = mystery part, 6 pins [chip_label="PM Sensor"]

nets:
  N1: M1.5V, M1.ISCP_5V, U1.pin6
  N2: M1.D2, U1.pin3
  N3: M1.GND, U1.pin5

custom parts:
  Arduino Uno WIFI REV2: The Arduino Uno WIFI REV2 is a microcontroller board based on the ATmega 4809. It has 14 digital input/output pins (of which 5 can be used as PWM outputs), 6 analog inputs, a 16 MHz ceramic resonator, a USB connection, a power jack, an ICSP header, and a reset button. It also has a WIFI controller with a secure ECC608 crypto unit and an internal IMU. It contains everything needed to support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
