# Fritzing sketch pmSesnor5VNeopixel (saved by Fritzing 0.9.9b)
breadboards: 1

parts:
  U1 = ESP32S-HiLetgo [part_number=ESP32S-HiLetgo]
  U2 = WS2812 RGB LED strip
  U3 = Mystery Part - 6 pins [chip_label="PM Sensor" package=THT]

nets:
  GND: U1.GPIO11, U2.GND, U3.GND
  VIN: U1.VIN, U2.VCC, U3.5V
  N1: U1.GPIO2, U2.DOUT
  N2: U1.GPIO0, U3.RX

notes:
  Gnd/Vin
  RX2/D4
  Gnd/5V
  RX

custom parts:
  ESP32S-HiLetgo: HiLetgo ESP-WROOM-32 ESP32 ESP-32S Development Board 2.4GHz Dual-Mode WiFi + Bluetooth Dual Cores Microcontroller The ESP32 integrated with Antenna switches, RF Balun, power amplifiers, low-noise amplifiers, filters, and management modules, and the entire solution occupies the least area of PCB. 2.4 GHz Wi-Fi plus Bluetooth dual-mode chip, with TSMC Ultra-low power consumption 40nm technology,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
  WS2812 RGB LED strip: WS2812 strip
  Mystery Part - 6 pins: A dummy, proxy, ersatz, stand-in part for whatever you want. With 6 pins on a 100 mil inline pin header footprint.
